# Fritzing sketch catapultDeclencheur (saved by Fritzing 0.9.2b)
breadboards: 1

parts:
  LTS-1720P = LTS-1720P [package=alphanumeric]
  Raspberry_Pi_B_rev1 = Raspberry Pi B rev1
  R6 = Resistor [tolerance=±5% resistance=220 package=THT]
  R7 = Resistor [tolerance=±5% resistance=220 package=THT]
  R8 = Resistor [tolerance=±5% resistance=220 package=THT]
  R5 = Resistor [tolerance=±5% resistance=220 package=THT]
  R4 = Resistor [tolerance=±5% resistance=220 package=THT]
  R3 = Resistor [tolerance=±5% resistance=220 package=THT]
  R2 = Resistor [tolerance=±5% resistance=220 package=THT]
  R1 = Resistor [tolerance=±5% resistance=220 package=THT]
  D1_1N4147 = Diode [package=diode-1n4148]
  D2 = Diode [package=diode-1n4148]
  D3 = Diode [package=diode-1n4148]
  S1 = Round Pushbutton
  SERVO_1 = Basic Servo
  BATT1 = 3xAAA Switchable Battery Pack w/JST connector

nets:
  N1: LTS-1720P.A, R1.Pin_1
  N2: LTS-1720P.F, R6.Pin_1
  N3: LTS-1720P.anode1, LTS-1720P.anode2, LTS-1720P.anode3, Raspberry_Pi_B_rev1.5V
  N4: LTS-1720P.E, R5.Pin_1
  N5: LTS-1720P.D, R4.Pin_1
  N6: LTS-1720P.DP, R8.Pin_1
  N7: LTS-1720P.C, R3.Pin_1
  N8: LTS-1720P.G, R7.Pin_1
  N9: LTS-1720P.B, R2.Pin_1
  GND: Raspberry_Pi_B_rev1.GND, S1.leg1, SERVO_1.gnd, BATT1.NEG
  N10: Raspberry_Pi_B_rev1.GPIO_23, R6.Pin_0
  N11: Raspberry_Pi_B_rev1.GPIO_18, SERVO_1.pulse
  N12: Raspberry_Pi_B_rev1.GPIO_22, S1.leg0
  N13: Raspberry_Pi_B_rev1.GPIO_24, R7.Pin_0
  N14: Raspberry_Pi_B_rev1.GPIO_10, R4.Pin_0
  N15: Raspberry_Pi_B_rev1.GPIO_9, R3.Pin_0
  N16: Raspberry_Pi_B_rev1.GPIO_25, D3.C
  N17: Raspberry_Pi_B_rev1.GPIO_11, R5.Pin_0
  N18: Raspberry_Pi_B_rev1.GPIO_8, R2.Pin_0
  N19: Raspberry_Pi_B_rev1.GPIO_7, R1.Pin_0
  N20: R8.Pin_0, D1_1N4147.A
  N21: D1_1N4147.C, D2.A
  N22: D2.C, D3.A
  N23: SERVO_1.vcc, BATT1.POS

custom parts:
  Diode: Diode These are standard reverse protection diodes and small signal diodes. SMA package can handle up to about 1A. SOD-323 can handle about 200mA. What the SOD-323 package when ordering, there are some mfgs out there that are 5-pin packages.
  3xAAA Switchable Battery Pack w/JST connector: 3xAAA Switchable Battery Pack with JST connector
